// Logisim project Shmerlard8.circ as structural Verilog: 7 circuits, main circuit main
module main (
  input  [15:0] in_1,
  input  RST,
  input  MAN,
  input  REG_RD,
  input  [2:0] in_5,
  input  REG_WR,
  input  [2:0] in_7,
  input  src_DST
);

  wire CLK;
  wire [15:0] register_file_1_data_out;

  Clock u_CLK (.out(CLK));
  register_file register_file_1 (
    .src_DST(src_DST), .REG_WR(REG_WR), .REG_RD(REG_RD), .CLK(CLK), .RST(RST), .REG_SEL_SRC(in_5),
    .REG_SEL_DST(in_7), .DATA_IN(register_file_1_data_out), .DATA_OUT(register_file_1_data_out));
  assign register_file_1_data_out = MAN ? in_1 : 16'bz;  // Controlled_Buffer controlled_buffer_1
  // Probe on register_file_1_data_out

  // Other names for the same wires on the sheet: REG_SEL_DST[2:0] = in_7; REG_SEL_SRC[2:0] = in_5
endmodule

module register_file (
  input  CLK,
  input  RST,
  input  [15:0] DATA_IN,
  input  REG_WR,
  input  [2:0] REG_SEL_SRC,
  input  [2:0] REG_SEL_DST,
  input  src_DST,
  input  REG_RD,
  output [15:0] DATA_OUT
);

  wire RD_EN_A, RD_EN_B, RD_EN_C, RD_EN_D, RD_EN_E, RD_EN_F, RD_EN_SP, RD_EN_SR, WR_EN_A, WR_EN_B, WR_EN_C,
       WR_EN_D, WR_EN_E, WR_EN_F, WR_EN_SP, WR_EN_SR;
  wire [2:0] multiplexer_1_out;
  wire [15:0] A_REG_q, B_REG_q, C_REG_q, D_REG_q, E_REG_q, F_REG_q, SP_REG_q, STATUS_REG_q;

  Hex_Digit_Display hex_digit_display_1 (.value({1'b0, REG_SEL_SRC}));  // open: dp
  Hex_Digit_Display hex_digit_display_2 (.value({1'b0, REG_SEL_DST}));  // open: dp
  Multiplexer #(.width(3)) multiplexer_1 (.in0(REG_SEL_SRC), .in1(REG_SEL_DST), .out(multiplexer_1_out), .sel(src_DST));
  // Probe on multiplexer_1_out
  Decoder #(.select(3)) decoder_1 (
    .out0(WR_EN_SP), .out1(WR_EN_SR), .out2(WR_EN_A), .out3(WR_EN_B), .out4(WR_EN_C), .out5(WR_EN_D),
    .out6(WR_EN_E), .out7(WR_EN_F), .sel(multiplexer_1_out), .en(REG_WR));
  Decoder #(.select(3)) decoder_2 (
    .out0(RD_EN_SP), .out1(RD_EN_SR), .out2(RD_EN_A), .out3(RD_EN_B), .out4(RD_EN_C), .out5(RD_EN_D),
    .out6(RD_EN_E), .out7(RD_EN_F), .sel(multiplexer_1_out), .en(REG_RD));
  Register #(.width(16)) SP_REG (.D(DATA_IN), .en(WR_EN_SP), .clk(CLK), .Q(SP_REG_q), .clr(RST));
  Register #(.width(16)) STATUS_REG (.D(DATA_IN), .en(WR_EN_SR), .clk(CLK), .Q(STATUS_REG_q), .clr(RST));
  Register #(.width(16)) A_REG (.D(DATA_IN), .en(WR_EN_A), .clk(CLK), .Q(A_REG_q), .clr(RST));
  Register #(.width(16)) B_REG (.D(DATA_IN), .en(WR_EN_B), .clk(CLK), .Q(B_REG_q), .clr(RST));
  Register #(.width(16)) C_REG (.D(DATA_IN), .en(WR_EN_C), .clk(CLK), .Q(C_REG_q), .clr(RST));
  Register #(.width(16)) D_REG (.D(DATA_IN), .en(WR_EN_D), .clk(CLK), .Q(D_REG_q), .clr(RST));
  Register #(.width(16)) E_REG (.D(DATA_IN), .en(WR_EN_E), .clk(CLK), .Q(E_REG_q), .clr(RST));
  Register #(.width(16)) F_REG (.D(DATA_IN), .en(WR_EN_F), .clk(CLK), .Q(F_REG_q), .clr(RST));
  assign DATA_OUT = RD_EN_SP ? SP_REG_q : 16'bz;  // Controlled_Buffer controlled_buffer_1
  assign DATA_OUT = RD_EN_SR ? STATUS_REG_q : 16'bz;  // Controlled_Buffer controlled_buffer_2
  assign DATA_OUT = RD_EN_A ? A_REG_q : 16'bz;  // Controlled_Buffer controlled_buffer_3
  assign DATA_OUT = RD_EN_B ? B_REG_q : 16'bz;  // Controlled_Buffer controlled_buffer_4
  assign DATA_OUT = RD_EN_C ? C_REG_q : 16'bz;  // Controlled_Buffer controlled_buffer_5
  assign DATA_OUT = RD_EN_D ? D_REG_q : 16'bz;  // Controlled_Buffer controlled_buffer_6
  assign DATA_OUT = RD_EN_E ? E_REG_q : 16'bz;  // Controlled_Buffer controlled_buffer_7
  assign DATA_OUT = RD_EN_F ? F_REG_q : 16'bz;  // Controlled_Buffer controlled_buffer_8
endmodule

module instruction_register (
  input  CLK,
  input  RST,
  input  IR_OUT,
  input  [15:0] D_BUS,
  input  IR_WR_EN,
  output [15:0] D_BUS_OUT,
  output [2:0] REG_SEL_DST,
  output [1:0] Add_DST,
  output [1:0] Add_SRC,
  output [2:0] REG_SEL_SRC,
  output [4:0] OP_CODE
);

  wire [3:3] IR_q;

  Register #(.width(16)) IR (
    .D(D_BUS), .en(IR_WR_EN), .clk(CLK), .Q({OP_CODE, REG_SEL_SRC, Add_SRC, Add_DST, IR_q[3], REG_SEL_DST}),
    .clr(CLK));
  assign D_BUS_OUT = IR_OUT ? {OP_CODE, REG_SEL_SRC, Add_SRC, Add_DST, IR_q[3], REG_SEL_DST} : 16'bz;  // Controlled_Buffer controlled_buffer_1

  // Other names for the same wires on the sheet: IR_L_O = IR_OUT
endmodule

module timing_control (
  input  TC_RST,
  input  CLK,
  output [4:0] T_OUT
);

  Counter #(.max('h1f), .width(5)) counter_1 (
    .clr(TC_RST), .load(1'b0), .up(1'b1), .count(1'b1), .clk(CLK), .Q(T_OUT));  // open: D, carry
endmodule

module memory_registers (
  input  CLK,
  input  RST,
  input  [15:0] D_BUS,
  input  MAR_WR_EN,
  input  [15:0] MEM_DATA_IN,
  input  MDR_WR_EN,
  input  MEM_sel,
  input  WR_sel,
  input  MDR_OUT_EN,
  output [15:0] MEM_ADDRESS_OUT,
  output [15:0] D_BUS_OUT,
  output [15:0] MEM_DATA_OUT,
  output RAM_WR_EN
);

  wire and_1_out, and_2_out, and_3_out, not_1_out, not_2_out;
  wire [15:0] controlled_buffer_1_out, MDR_q;

  assign controlled_buffer_1_out = not_1_out ? D_BUS : 16'bz;  // Controlled_Buffer controlled_buffer_1
  Register #(.width(16)) MAR (.D(D_BUS), .en(MAR_WR_EN), .clk(CLK), .Q(MEM_ADDRESS_OUT), .clr(RST));
  not not_1 (not_1_out, MEM_sel);
  assign controlled_buffer_1_out = and_1_out ? MEM_DATA_IN : 16'bz;  // Controlled_Buffer controlled_buffer_2
  Register #(.width(16)) MDR (.D(controlled_buffer_1_out), .en(MDR_WR_EN), .clk(CLK), .Q(MDR_q), .clr(RST));
  not not_2 (not_2_out, WR_sel);
  and and_1 (and_1_out, MEM_sel, not_2_out);
  assign MEM_DATA_OUT = and_2_out ? MDR_q : 16'bz;  // Controlled_Buffer controlled_buffer_3
  and and_2 (and_2_out, WR_sel, MDR_OUT_EN);
  and and_3 (and_3_out, not_1_out, MDR_OUT_EN);
  assign D_BUS_OUT = and_3_out ? MDR_q : 16'bz;  // Controlled_Buffer controlled_buffer_4

  assign RAM_WR_EN = WR_sel;
endmodule

module program_counter (
  input  CLK,
  input  RST,
  input  PC_OUT_EN,
  input  PC_WR_EN,
  input  PC_INC_EN,
  input  [15:0] D_BUS,
  output [15:0] D_BUS_OUT
);

  wire [15:0] counter_1_q;

  Counter #(.max('hffff), .width(16)) counter_1 (
    .clr(RST), .load(PC_WR_EN), .up(1'b1), .count(PC_INC_EN), .clk(CLK), .D(D_BUS), .Q(counter_1_q));  // open: carry
  assign D_BUS_OUT = PC_OUT_EN ? counter_1_q : 16'bz;  // Controlled_Buffer controlled_buffer_1
endmodule

module alu (
  input  [3:0] RLC_AMOUNT,
  input  CLK,
  input  RST,
  input  [3:0] SHRA_AMOUNT,
  input  [15:0] D_BUS,
  input  [2:0] ALU_MUX,
  input  [3:0] Flags,
  input  Y_WR_EN,
  input  Y_OUT,
  output [15:0] D_BUS_OUT
);

  wire [15:0] multiplexer_1_out, X1, Y_ADD, Y_REG_q, Y_SHRA, Y_SUB;

  Register #(.width(16)) X_REG (.D(D_BUS), .clk(CLK), .Q(X1), .clr(RST));  // open: en
  // Probe on Y_ADD
  Adder #(.width(16)) adder_1 (.a(D_BUS), .b(X1), .out(Y_ADD));  // open: cin, cout
  // Probe on Y_SUB
  Subtractor #(.width(16)) subtractor_1 (.a(D_BUS), .b(X1), .out(Y_SUB));  // open: bin, bout
  Multiplexer #(.select(3), .width(16)) multiplexer_1 (
    .in0(Y_SHRA), .in1(Y_SHRA), .in2(Y_ADD), .in3(Y_SUB), .out(multiplexer_1_out), .sel(ALU_MUX));  // open: in4, in5, in6, in7
  // Probe on Y_SHRA
  Shifter #(.shift("lr"), .width(16)) shifter_1 (.in(D_BUS), .\dist (RLC_AMOUNT), .out(Y_SHRA));
  // Probe on Y_SHRA
  Shifter #(.shift("rr"), .width(16)) shifter_2 (.in(D_BUS), .\dist (SHRA_AMOUNT), .out(Y_SHRA));
  Register #(.width(16)) Y_REG (.D(multiplexer_1_out), .en(Y_WR_EN), .clk(CLK), .Q(Y_REG_q), .clr(RST));
  assign D_BUS_OUT = Y_OUT ? Y_REG_q : 16'bz;  // Controlled_Buffer controlled_buffer_1

  // Other names for the same wires on the sheet: X2[15:0] = D_BUS
endmodule
